# Fritzing sketch tnt_game_electronics (saved by Fritzing 0.9.4)

parts:
  S1 = Toggle Switch [package=THT]
  VCC2 = 4 x AAA Battery Mount
  Keypad4x1 = Keypad Membran 4x4
  Part1 = Arduino Uno (Rev3)
  Grove1 = Grove OLED 128x96
  J1 = Piezo Speaker
  U1 = 2.5mm Audio Jack [package=stereojack2.5mm_smd]
  U2 = 2.5mm Audio Jack [package=stereojack2.5mm_smd]
  U3 = 2.5mm Audio Jack [package=stereojack2.5mm_smd]  # not connected
  U4 = 2.5mm Audio Jack [package=stereojack2.5mm_smd]  # not connected
  U5 = 2.5mm Audio Jack [package=stereojack2.5mm_smd]  # not connected
  U6 = 2.5mm Audio Jack [package=stereojack2.5mm_smd]  # not connected

nets:
  N1: S1.L1, VCC2.+
  N2: S1.L2, Part1.VIN
  GND: VCC2.-, Part1.GND, Grove1.GND, J1.pin1
  N3: Keypad4x1.Pin1, Part1.D9_PWM
  N4: Keypad4x1.Pin2, Part1.D8
  N5: Keypad4x1.Pin3, Part1.D7
  N6: Keypad4x1.Pin4, Part1.D6_PWM
  N7: Keypad4x1.Pin5, Part1.D5_PWM
  N8: Keypad4x1.Pin6, Part1.D4
  N9: Keypad4x1.Pin7, Part1.D3_PWM
  N10: Keypad4x1.Pin8, Part1.D2
  N11: Part1.D10_PWM/SS, J1.pin2
  N12: Part1.D12/MISO, U2.RIGHT
  N13: Part1.D13/SCK, U1.RIGHT
  N14: Part1.A4/SDA, Grove1.SDA
  N15: Part1.A5/SCL, Grove1.SCL
  5V: Part1.5V, Grove1.VCC

notes:
  Can't find the 2.5mm headphone plug so pretend above is that

custom parts:
  Keypad Membran 4x4: Membrane Keypad 4x4 Matrix
